# Fritzing sketch printplaatRaspberry (saved by Fritzing 0.9.3b)
circuit board: 6.04455cm x 4.62293cm
breadboards: 1

parts:
  Raspberry_Pi_1 = Raspberry Pi 3 [part_number=RPI-3-V1.2]
  LED1 = LED - 5mm [color="Red (633nm)" package="5 mm [THT]"]
  R1 = Resistor [tolerance=±5% resistance=220 package=THT]
  LED2 = LED - 5mm [color="Red (633nm)" package="5 mm [THT]"]
  LED3 = LED - 5mm [color="Red (633nm)" package="5 mm [THT]"]
  R2 = Resistor [tolerance=±5% resistance=220 package=THT]
  R3 = Resistor [tolerance=±5% resistance=220 package=THT]
  JP1 = Header 12 [package=1x12_machine-pin-header_lock.004]

nets:
  3V3: Raspberry_Pi_1.3v3, Raspberry_Pi_1.3V3, JP1.12
  N1: Raspberry_Pi_1.GPIO4, JP1.7
  N2: Raspberry_Pi_1.GND, R1.Pin_0, R2.Pin_0, R3.Pin_0, JP1.11
  N3: Raspberry_Pi_1.GPIO27, JP1.6
  N4: Raspberry_Pi_1.GPIO22, JP1.5
  N5: Raspberry_Pi_1.GPIO10, LED3.anode, JP1.10
  N6: Raspberry_Pi_1.GPIO9, LED2.anode, JP1.9
  N7: Raspberry_Pi_1.GPIO11, LED1.anode, JP1.8
  N8: LED1.cathode, R1.Pin_1
  N9: LED2.cathode, R3.Pin_1
  N10: LED3.cathode, R2.Pin_1
